# Fritzing sketch Radiodan_app2 (saved by Fritzing 0.8.3b)
breadboards: 1

parts:
  RaspberryPi1 = Raspberry Pi Model B
  R1 = Rotary Potentiometer (Small)
  S1 = Round Pushbutton
  S2 = Round Pushbutton
  S3 = Round Pushbutton

nets:
  N1: RaspberryPi1.#17, S1.leg0
  N2: RaspberryPi1.#22, S3.leg1
  N3: RaspberryPi1.#23, R1.leg1
  N4: RaspberryPi1.#24, R1.leg2
  N5: RaspberryPi1.#25, S2.leg0
  N6: R1.wiper, S1.leg1, S2.leg1, S3.leg0

notes:
  next station
  previous station
  anticlockwise->lower volume
  clockwise->higher volume
  avoid

custom parts:
  Raspberry Pi Model B: Raspberry Pi (Model B)
